// Logisim project CO Basic Computer Bus System Simulator.circ as structural Verilog: 12 circuits, main circuit main
module main (
);

  wire bus_1_e, clock_1_out, control_unit_1_ac_clear, control_unit_1_ac_com, control_unit_1_ac_increment,
       control_unit_1_ac_load, control_unit_1_add, control_unit_1_and, control_unit_1_ar_clear,
       control_unit_1_ar_increment, control_unit_1_ar_load, control_unit_1_cil, control_unit_1_cir,
       control_unit_1_dr_2, control_unit_1_dr_clear, control_unit_1_dr_increment, control_unit_1_dr_load,
       control_unit_1_e_com, control_unit_1_ir_load, control_unit_1_memory_read, control_unit_1_memory_write,
       control_unit_1_pc_clear, control_unit_1_pc_increment, control_unit_1_pc_load;
  wire [2:0] control_unit_1_bus_selector;
  wire [11:0] counter_1_q;
  wire [15:0] bus_1_ac, bus_1_dr_2, bus_1_ir, bus_1_m_ar;

  Control_Unit control_unit_1 (
    .IR(bus_1_ir), .Bus_selector(control_unit_1_bus_selector), .AND(control_unit_1_and),
    .AC_Com(control_unit_1_ac_com), .CIL(control_unit_1_cil), .CIR(control_unit_1_cir),
    .ADD(control_unit_1_add), .DR_2(control_unit_1_dr_2), .E_Com(control_unit_1_e_com), .AC(bus_1_ac),
    .E(bus_1_e), .DR(bus_1_dr_2), .PC_Load(control_unit_1_pc_load),
    .PC_Increment(control_unit_1_pc_increment), .PC_Clear(control_unit_1_pc_clear),
    .DR_Load(control_unit_1_dr_load), .DR_Increment(control_unit_1_dr_increment),
    .DR_Clear(control_unit_1_dr_clear), .AR_Load(control_unit_1_ar_load),
    .AR_Increment(control_unit_1_ar_increment), .AR_Clear(control_unit_1_ar_clear),
    .AC_Load(control_unit_1_ac_load), .AC_Increment(control_unit_1_ac_increment),
    .AC_Clear(control_unit_1_ac_clear), .IR_Load(control_unit_1_ir_load),
    .Memory_Read(control_unit_1_memory_read), .Memory_Write(control_unit_1_memory_write));
  BUS bus_1 (
    .LDAR(control_unit_1_ar_load), .INAR(control_unit_1_ar_increment), .LDPC(control_unit_1_pc_load),
    .INPC(control_unit_1_pc_increment), .LDDR(control_unit_1_dr_load), .INDR(control_unit_1_dr_increment),
    .LDAC(control_unit_1_ac_load), .INAC(control_unit_1_ac_increment), .LDIR(control_unit_1_ir_load),
    .LDTR(1'b0), .INTR(1'b0), .AND(control_unit_1_and), .COM(control_unit_1_ac_com),
    .CIL(control_unit_1_cil), .CIR(control_unit_1_cir), .ADD(control_unit_1_add), .DR(control_unit_1_dr_2),
    .write(control_unit_1_memory_write), .CLRAR(control_unit_1_ar_clear), .CLRTR(1'b0),
    .CLRPC(control_unit_1_pc_clear), .CLRDR(control_unit_1_dr_clear), .CLRAC(control_unit_1_ac_clear),
    .read(control_unit_1_memory_read), .E_Comp(control_unit_1_e_com), .E(bus_1_e), .AC(bus_1_ac),
    .DR_2(bus_1_dr_2), .IR(bus_1_ir), .M_AR(bus_1_m_ar), .BUS_SEL(control_unit_1_bus_selector),
    .in_1(counter_1_q));
  Hex_Digit_Display hex_digit_display_1 (.value(bus_1_m_ar[15:12]));  // open: dp
  Hex_Digit_Display hex_digit_display_2 (.value(bus_1_m_ar[11:8]));  // open: dp
  Hex_Digit_Display hex_digit_display_3 (.value(bus_1_m_ar[7:4]));  // open: dp
  Counter #(.width(12), .max('hfff)) counter_1 (
    .count(1'b0), .Q(counter_1_q), .clk(clock_1_out));  // open: load, D, carry, clr
  Clock clock_1 (.out(clock_1_out));
  Hex_Digit_Display hex_digit_display_4 (.value(bus_1_m_ar[3:0]));  // open: dp

  // Notes on the sheet:
  //   After the program halts Just input the address of the
  //   required memory location
  //   and the value will be displayed
  //   in the LED screen
endmodule

module ALU (
  input  [15:0] AC,
  input  [15:0] DR,
  input  AND,
  input  COM,
  input  ADD,
  input  Transfer_DR,
  input  CIL,
  input  CIR,
  output [15:0] AC_2,
  output V,
  output E
);

  wire bitselector_1_out, bitselector_2_out;
  wire [3:0] priority_encoder_1_out;
  wire [15:0] adder_1_out, adder_2_out, AND_out, NOT_out, OR_out, shifter_1_out, shifter_2_out,
       shifter_3_out, shifter_4_out, shifter_5_out, shifter_6_out, subtractor_1_out, subtractor_2_out,
       XOR_out;

  assign AND_out = AC & DR;  // AND_Gate AND, 16 bits wide
  assign OR_out = AC | DR;  // OR_Gate OR, 16 bits wide
  assign XOR_out = AC ^ DR;  // XOR_Gate XOR, 16 bits wide
  assign NOT_out = ~AC;  // NOT_Gate NOT, 16 bits wide
  Shifter #(.width(16)) shifter_1 (.in(AC), .\dist (4'b0001), .out(shifter_1_out));
  Shifter #(.width(16), .shift("lr")) shifter_2 (.in(AC), .\dist (4'b0001), .out(shifter_2_out));
  Shifter #(.width(16), .shift("rl")) shifter_3 (.in(AC), .\dist (4'b0001), .out(shifter_3_out));
  Shifter #(.width(16), .shift("rr")) shifter_4 (.in(AC), .\dist (4'b0001), .out(shifter_4_out));
  BitSelector #(.width(16)) bitselector_1 (.in(AC), .out(bitselector_1_out), .sel(4'b1111));
  BitSelector #(.width(16)) bitselector_2 (.in(AC), .out(bitselector_2_out), .sel(4'b1110));
  Shifter #(.width(16)) shifter_5 (.in(AC), .\dist (4'b0001), .out(shifter_5_out));
  Shifter #(.width(16), .shift("ar")) shifter_6 (.in(AC), .\dist (4'b0001), .out(shifter_6_out));
  Adder #(.width(16)) adder_1 (.a(AC), .b(DR), .out(adder_1_out), .cin(1'b0), .cout(E));
  Subtractor #(.width(16)) subtractor_1 (.a(AC), .b(DR), .out(subtractor_1_out), .bin(1'b0));  // open: bout
  Adder #(.width(16)) adder_2 (.a(AC), .b(16'h1), .out(adder_2_out), .cin(1'b0));  // open: cout
  Subtractor #(.width(16)) subtractor_2 (.a(AC), .b(16'h1), .out(subtractor_2_out), .bin(1'b0));  // open: bout
  xor xor_2 (V, bitselector_1_out, bitselector_2_out);
  Multiplexer #(.select(4), .width(16), .enable("false")) multiplexer_1 (
    .in0(AND_out), .in1(OR_out), .in2(XOR_out), .in3(NOT_out), .in4(shifter_1_out), .in5(shifter_2_out),
    .in6(shifter_3_out), .in7(shifter_4_out), .in8(shifter_5_out), .in9(shifter_6_out), .in10(adder_1_out),
    .in11(subtractor_1_out), .in12(adder_2_out), .in13(subtractor_2_out), .in14(AC), .in15(DR), .out(AC_2),
    .sel(priority_encoder_1_out));
  Priority_Encoder #(.select(4)) priority_encoder_1 (
    .in0(AND), .in1(1'b0), .in2(1'b0), .in3(COM), .in4(1'b0), .in5(1'b0), .in6(CIL), .in7(CIR), .in8(1'b0),
    .in9(1'b0), .in10(ADD), .in11(1'b0), .in12(1'b0), .in13(1'b0), .in14(1'b0), .in15(Transfer_DR),
    .out(priority_encoder_1_out));

  // Other names for the same wires on the sheet: c_add = E

  // Notes on the sheet:
  //   LSL
  //   LSR
  //   CSL
  //   CSR
  //   ASL
  //   ASR
  //   ADD
  //   SUB
  //   INC
  //   DEC
  //   Transfer AC
  //   Transfer DR
  //   Over Flow of ASL
  //   The role of the encoder is to 
  //   convert the control signals to selection lines
  //   so, in the process, the arithmetic/ logical/ shift operations
  //   that are not present inside the BC ALU
  //   were replaced witha constant signal of 0
  //   since they can never be selected
endmodule

module BUS (
  input  [11:0] in_1,
  input  write,
  input  read,
  input  LDAR,
  input  INAR,
  input  CLRAR,
  input  LDPC,
  input  INPC,
  input  CLRPC,
  input  [2:0] BUS_SEL,
  input  LDDR,
  input  INDR,
  input  CLRDR,
  input  LDAC,
  input  AND,
  input  INAC,
  input  E_Comp,
  input  CIL,
  input  DR,
  input  COM,
  input  CIR,
  input  CLRAC,
  input  ADD,
  input  LDIR,
  input  LDTR,
  input  INTR,
  input  CLRTR,
  output [15:0] M_AR,
  output [15:0] DR_2,
  output E,
  output [15:0] AC,
  output [15:0] IR
);

  wire alu_1_e, clk, comparator_1_eq, d_ff_1_q, not_1_out, not_2_out, or_1_out, or_2_out, or_3_out;
  wire [11:0] AR_q, bit_extender_1_out, bit_extender_2_out, controlled_buffer_1_out, PC_q;
  wire [15:0] alu_1_ac_2, bit_extender_3_out, bit_extender_4_out, multiplexer_1_out, TR_q;

  assign controlled_buffer_1_out = comparator_1_eq ? in_1 : 12'bz;  // Controlled_Buffer controlled_buffer_1
  Comparator #(.width(16), .mode("unsigned")) comparator_1 (
    .a(IR), .b(16'h7001), .eq(comparator_1_eq));  // open: gt, lt
  ALU alu_1 (
    .AC(AC), .DR(DR_2), .AC_2(alu_1_ac_2), .E(alu_1_e), .AND(AND), .COM(COM), .CIR(CIR), .ADD(ADD),
    .Transfer_DR(DR), .CIL(CIL));  // open: V
  assign controlled_buffer_1_out = not_1_out ? AR_q : 12'bz;  // Controlled_Buffer controlled_buffer_2
  not not_1 (not_1_out, comparator_1_eq);
  not not_2 (not_2_out, alu_1_e);
  Bit_Extender #(.in_width(16), .out_width(12)) bit_extender_1 (.in(multiplexer_1_out), .out(bit_extender_1_out));
  Bit_Extender #(.in_width(16), .out_width(12)) bit_extender_2 (.in(multiplexer_1_out), .out(bit_extender_2_out));
  or or_1 (or_1_out, alu_1_e, E_Comp);
  or or_2 (or_2_out, not_2_out, E_Comp);
  J_K_Flip_Flop j_k_ff_1 (
    .J(or_1_out), .clk(clk), .K(or_2_out), .Q(E), .preset(1'b0), .en(ADD), .reset(1'b0));  // open: Qn
  or or_3 (or_3_out, comparator_1_eq, read);
  Counter #(.width(12), .max('hfff)) AR (
    .load(LDAR), .D(bit_extender_1_out), .count(INAR), .Q(AR_q), .clk(clk), .clr(CLRAR));  // open: carry
  Counter #(.width(12), .max('hfff)) PC (
    .load(LDPC), .D(bit_extender_2_out), .count(INPC), .Q(PC_q), .clk(clk), .clr(CLRPC));  // open: carry
  Counter #(.width(16), .max('hffff)) counter_1 (
    .load(LDDR), .D(multiplexer_1_out), .count(INDR), .Q(DR_2), .clk(clk), .clr(CLRDR));  // open: carry
  Counter #(.width(16), .max('hffff)) counter_2 (
    .load(LDAC), .D(alu_1_ac_2), .count(INAC), .Q(AC), .clk(clk), .clr(d_ff_1_q));  // open: carry
  D_Flip_Flop d_ff_1 (.clk(clk), .D(CLRAC), .Q(d_ff_1_q), .en(1'b1));  // open: Qn, preset, reset
  Counter #(.width(16), .max('hffff)) u_IR (
    .load(LDIR), .D(multiplexer_1_out), .count(1'b0), .Q(IR), .clk(clk), .clr(1'b0));  // open: carry
  Counter #(.width(16), .max('hffff)) TR (
    .load(LDTR), .D(multiplexer_1_out), .count(INTR), .Q(TR_q), .clk(clk), .clr(CLRTR));  // open: carry
  RAM #(.addrWidth(12), .dataWidth(16), .bus("separate")) ram_1 (
    .addr(controlled_buffer_1_out), .din(multiplexer_1_out), .data(M_AR), .str(write), .sel(1'b1), .clk(clk),
    .ld(or_3_out), .clr(1'b0));
  assign bit_extender_3_out = {{4{1'b0}}, AR_q};  // Bit_Extender bit_extender_3
  assign bit_extender_4_out = {{4{1'b0}}, PC_q};  // Bit_Extender bit_extender_4
  Clock clock_1 (.out(clk));
  Multiplexer #(.select(3), .width(16), .enable("false")) multiplexer_1 (
    .in1(bit_extender_3_out), .in2(bit_extender_4_out), .in3(DR_2), .in4(AC), .in5(IR), .in6(TR_q),
    .in7(M_AR), .out(multiplexer_1_out), .sel(BUS_SEL));  // open: in0

  // Other names for the same wires on the sheet: M[15:0] = M_AR

  // Notes on the sheet:
  //   MEM
  //   DR
  //   AC
endmodule

module Control_Unit (
  input  [15:0] IR,
  input  E,
  input  [15:0] AC,
  input  [15:0] DR,
  output [2:0] Bus_selector,
  output AR_Load,
  output AR_Increment,
  output AR_Clear,
  output AND,
  output AC_Com,
  output CIL,
  output CIR,
  output ADD,
  output DR_2,
  output E_Com,
  output PC_Load,
  output DR_Load,
  output PC_Increment,
  output DR_Increment,
  output PC_Clear,
  output DR_Clear,
  output AC_Load,
  output IR_Load,
  output AC_Increment,
  output AC_Clear,
  output Memory_Read,
  output Memory_Write
);

  wire and_1_out, B0, B1, B2, B3, B4, B5, B6, B7, B8, B9, B10, B11, CLK, D0, D1, D2, D3, D4, D5, D6, D7, I,
       not_1_out, S, SC, sc_1_sc_clear, T0, T2, T3, T4, T5, T6, T7, T8, T9, T10, T11, T12, T13, T14, T15,
       t_ff_1_q;
  wire [3:0] counter_1_q;
  wire [14:12] counter_2_q;

  Clock clock_1 (.out(CLK));
  Decoder #(.select(4), .enable("false")) decoder_1 (
    .out0(T0), .out1(IR_Load), .out2(T2), .out3(T3), .out4(T4), .out5(T5), .out6(T6), .out7(T7), .out8(T8),
    .out9(T9), .out10(T10), .out11(T11), .out12(T12), .out13(T13), .out14(T14), .out15(T15), .sel(counter_1_q));
  Counter #(.width(4), .max('hf)) counter_1 (
    .count(1'b1), .Q(counter_1_q), .clk(CLK), .clr(S));  // open: load, D, carry
  Decoder #(.select(3), .enable("false")) decoder_2 (
    .out0(D0), .out1(D1), .out2(D2), .out3(D3), .out4(D4), .out5(D5), .out6(D6), .out7(D7), .sel(counter_2_q));
  D_Flip_Flop u_I (.clk(CLK), .D(IR[15]), .Q(I), .en(T2));  // open: Qn, preset, reset
  Counter #(.width(15), .max('h7fff)) counter_2 (
    .load(T2), .D(IR[14:0]), .count(1'b0),
    .Q({counter_2_q, B11, B10, B9, B8, B7, B6, B5, B4, B3, B2, B1, B0}), .clk(CLK));  // open: carry, clr
  PC_Control pc_control_1 (
    .D0(D0), .D1(D1), .D2(D2), .D3(D3), .D4(D4), .D5(D5), .D6(D6), .D7(D7), .T0(T0), .T1(IR_Load), .T2(T2),
    .T3(T3), .T4(T4), .T5(T5), .T6(T6), .T7(T7), .T8(T8), .T9(T9), .T10(T10), .T11(T11), .T12(T12),
    .T13(T13), .T14(T14), .T15(T15), .I(I), .B0(B0), .B1(B1), .B2(B2), .B3(B3), .B4(B4), .B5(B5), .B6(B6),
    .B7(B7), .B8(B8), .B9(B9), .B10(B10), .B11(B11), .E(E), .AC(AC), .DR(DR), .PC_Load(PC_Load),
    .PC_Increment(PC_Increment), .PC_Clear(PC_Clear));
  Bus_Control bus_control_1 (
    .D0(D0), .D1(D1), .D2(D2), .D3(D3), .D4(D4), .D5(D5), .D6(D6), .D7(D7), .T0(T0), .T1(IR_Load), .T2(T2),
    .T3(T3), .T4(T4), .T5(T5), .T6(T6), .T7(T7), .T8(T8), .T9(T9), .T10(T10), .T11(T11), .T12(T12),
    .T13(T13), .T14(T14), .T15(T15), .I(I), .out_26(Bus_selector));
  AC_Control ac_control_1 (
    .D0(D0), .D1(D1), .D2(D2), .D3(D3), .D4(D4), .D5(D5), .D6(D6), .D7(D7), .T0(T0), .T1(IR_Load), .T2(T2),
    .T3(T3), .T4(T4), .T5(T5), .T6(T6), .T7(T7), .T8(T8), .T9(T9), .T10(T10), .T11(T11), .T12(T12),
    .T13(T13), .T14(T14), .T15(T15), .I(I), .B0(B0), .B1(B1), .B2(B2), .B3(B3), .B4(B4), .B5(B5), .B6(B6),
    .B7(B7), .B8(B8), .B9(B9), .B10(B10), .B11(B11), .AC_Load(AC_Load), .AC_Increment(AC_Increment),
    .AC_Clear(AC_Clear));
  ALU_Control alu_control_1 (
    .D0(D0), .D1(D1), .D2(D2), .D3(D3), .D4(D4), .D5(D5), .D6(D6), .D7(D7), .T0(T0), .T1(IR_Load), .T2(T2),
    .T3(T3), .T4(T4), .T5(T5), .T6(T6), .T7(T7), .T8(T8), .T9(T9), .T10(T10), .T11(T11), .T12(T12),
    .T13(T13), .T14(T14), .T15(T15), .I(I), .B0(B0), .B1(B1), .B2(B2), .B3(B3), .B4(B4), .B5(B5), .B6(B6),
    .B7(B7), .B8(B8), .B9(B9), .B10(B10), .B11(B11), .AND(AND), .AC_Com(AC_Com), .CIL(CIL), .CIR(CIR),
    .ADD(ADD), .DR(DR_2), .E_Com(E_Com));
  AR_Control ar_control_1 (
    .D0(D0), .D1(D1), .D2(D2), .D3(D3), .D4(D4), .D5(D5), .D6(D6), .D7(D7), .T0(T0), .T1(IR_Load), .T2(T2),
    .T3(T3), .T4(T4), .T5(T5), .T6(T6), .T7(T7), .T8(T8), .T9(T9), .T10(T10), .T11(T11), .T12(T12),
    .T13(T13), .T14(T14), .T15(T15), .I(I), .AR_Load(AR_Load), .AR_Increment(AR_Increment),
    .AR_Clear(AR_Clear));
  DR_Control dr_control_1 (
    .D0(D0), .D1(D1), .D2(D2), .D3(D3), .D4(D4), .D5(D5), .D6(D6), .D7(D7), .T0(T0), .T1(IR_Load), .T2(T2),
    .T3(T3), .T4(T4), .T5(T5), .T6(T6), .T7(T7), .T8(T8), .T9(T9), .T10(T10), .T11(T11), .T12(T12),
    .T13(T13), .T14(T14), .T15(T15), .DR_Load(DR_Load), .DR_Increment(DR_Increment), .DR_Clear(DR_Clear));
  Memory_Control memory_control_1 (
    .D0(D0), .D1(D1), .D2(D2), .D3(D3), .D4(D4), .D5(D5), .D6(D6), .D7(D7), .T0(T0), .T1(IR_Load), .T2(T2),
    .T3(T3), .T4(T4), .T5(T5), .T6(T6), .T7(T7), .T8(T8), .T9(T9), .T10(T10), .T11(T11), .T12(T12),
    .T13(T13), .T14(T14), .T15(T15), .Memory_Read(Memory_Read), .Memory_Write(Memory_Write), .I(I));
  not not_1 (not_1_out, I);
  SC sc_1 (
    .D0(D0), .D1(D1), .D2(D2), .D3(D3), .D4(D4), .D5(D5), .D6(D6), .D7(D7), .T0(T0), .T1(IR_Load), .T2(T2),
    .T3(T3), .T4(T4), .T5(T5), .T6(T6), .T7(T7), .T8(T8), .T9(T9), .T10(T10), .T11(T11), .T12(T12),
    .T13(T13), .T14(T14), .T15(T15), .I(I), .SC_Clear(sc_1_sc_clear));
  and and_1 (and_1_out, D7, not_1_out, T3, B0);
  D_Flip_Flop d_ff_1 (.clk(CLK), .D(sc_1_sc_clear), .Q(SC), .en(1'b1));  // open: Qn, preset, reset
  T_Flip_Flop t_ff_1 (.clk(CLK), .T(and_1_out), .Q(t_ff_1_q), .en(1'b1));  // open: Qn, preset, reset
  or or_1 (S, t_ff_1_q, SC);

  // Other names for the same wires on the sheet: Bi[11:0] = {B11, B10, B9, B8, B7, B6, B5, B4, B3, B2, B1, B0};
  //   T1 = IR_Load

  // Notes on the sheet:
  //   To Halt the program and Stop the clock forever
endmodule

module Bus_Control (
  input  D0,
  input  D1,
  input  D2,
  input  D3,
  input  D4,
  input  D5,
  input  D6,
  input  D7,
  input  T0,
  input  T1,
  input  T2,
  input  T3,
  input  T4,
  input  T5,
  input  T6,
  input  T7,
  input  T8,
  input  T9,
  input  T10,
  input  T11,
  input  T12,
  input  T13,
  input  T14,
  input  T15,
  input  I,
  output [2:0] out_26
);

  wire AC_out, and_1_out, and_2_out, and_3_out, and_4_out, and_5_out, and_6_out, and_7_out, and_8_out,
       AR_B_out, DR_out, Memory_out, not_1_out, PC_B_out;

  not not_1 (not_1_out, D7);
  and and_1 (and_1_out, not_1_out, I, T3);
  and and_2 (and_2_out, D0, T4);
  and and_3 (and_3_out, D1, T4);
  and and_4 (and_4_out, D2, T4);
  and and_5 (and_5_out, D6, T4);
  and and_6 (and_6_out, D4, T4);
  or AR_B (AR_B_out, and_6_out, and_7_out);
  and and_7 (and_7_out, D5, T5);
  or PC_B (PC_B_out, T0, and_8_out);
  and and_8 (and_8_out, D5, T4);
  and DR (DR_out, D6, T6);
  and AC (AC_out, D3, T4);
  or Memory (Memory_out, T1, and_1_out, and_2_out, and_3_out, and_4_out, and_5_out);
  Priority_Encoder priority_encoder_1 (
    .in0(1'b0), .in1(AR_B_out), .in2(PC_B_out), .in3(DR_out), .in4(AC_out), .in5(T2), .in6(1'b0),
    .in7(Memory_out), .out(out_26), .en_in(1'b1));  // open: gs, en_out
endmodule

module ALU_Control (
  input  D0,
  input  D1,
  input  D2,
  input  D3,
  input  D4,
  input  D5,
  input  D6,
  input  D7,
  input  T0,
  input  T1,
  input  T2,
  input  T3,
  input  T4,
  input  T5,
  input  T6,
  input  T7,
  input  T8,
  input  T9,
  input  T10,
  input  T11,
  input  T12,
  input  T13,
  input  T14,
  input  T15,
  input  I,
  input  B0,
  input  B1,
  input  B2,
  input  B3,
  input  B4,
  input  B5,
  input  B6,
  input  B7,
  input  B8,
  input  B9,
  input  B10,
  input  B11,
  output AND,
  output AC_Com,
  output CIL,
  output CIR,
  output ADD,
  output DR,
  output E_Com
);

  wire not_1_out, r;

  not not_1 (not_1_out, I);
  and u_R (r, D7, not_1_out, T3);
  and u_AND (AND, D0, T5);
  and u_AC_Com (AC_Com, r, B9);
  and u_CIL (CIL, r, B6);
  and u_CIR (CIR, r, B7);
  and u_ADD (ADD, D1, T5);
  and u_DR (DR, D2, T5);
  and u_E_Com (E_Com, r, B8);
endmodule

module PC_Control (
  input  D0,
  input  D1,
  input  D2,
  input  D3,
  input  D4,
  input  D5,
  input  D6,
  input  D7,
  input  T0,
  input  T1,
  input  T2,
  input  T3,
  input  T4,
  input  T5,
  input  T6,
  input  T7,
  input  T8,
  input  T9,
  input  T10,
  input  T11,
  input  T12,
  input  T13,
  input  T14,
  input  T15,
  input  I,
  input  B0,
  input  B1,
  input  B2,
  input  B3,
  input  B4,
  input  B5,
  input  B6,
  input  B7,
  input  B8,
  input  B9,
  input  B10,
  input  B11,
  input  E,
  input  [15:0] AC,
  input  [15:0] DR,
  output PC_Load,
  output PC_Increment,
  output PC_Clear
);

  wire and_1_out, and_2_out, and_3_out, and_4_out, and_5_out, and_6_out, and_7_out, and_8_out, and_9_out,
       comparator_1_eq, comparator_2_eq, not_1_out, not_2_out, not_3_out, or_2_out, r;

  not not_1 (not_1_out, I);
  and u_R (r, D7, not_1_out, T3);
  Comparator #(.width(16)) comparator_1 (.a(AC), .b({16{1'b0}}), .eq(comparator_1_eq));  // open: gt, lt
  not not_2 (not_2_out, E);
  and and_1 (and_1_out, not_2_out, B1);
  and and_2 (and_2_out, comparator_1_eq, B2);
  and and_3 (and_3_out, AC[15], B3);
  not not_3 (not_3_out, AC[15]);
  and and_4 (and_4_out, not_3_out, B4);
  and and_5 (and_5_out, D4, T4);
  and and_6 (and_6_out, D5, T5);
  or or_1 (PC_Load, and_5_out, and_6_out);
  or or_2 (or_2_out, and_1_out, and_2_out, and_3_out, and_4_out);
  and and_7 (and_7_out, D6, T6);
  Comparator #(.width(16), .mode("unsigned")) comparator_2 (
    .a(DR), .b({16{1'b0}}), .eq(comparator_2_eq));  // open: gt, lt
  and and_8 (and_8_out, r, or_2_out);
  and and_9 (and_9_out, and_7_out, comparator_2_eq);
  or or_3 (PC_Increment, T1, and_8_out, and_9_out);

  assign PC_Clear = 1'b0;
endmodule

module DR_Control (
  input  D0,
  input  D1,
  input  D2,
  input  D3,
  input  D4,
  input  D5,
  input  D6,
  input  D7,
  input  T0,
  input  T1,
  input  T2,
  input  T3,
  input  T4,
  input  T5,
  input  T6,
  input  T7,
  input  T8,
  input  T9,
  input  T10,
  input  T11,
  input  T12,
  input  T13,
  input  T14,
  input  T15,
  output DR_Load,
  output DR_Increment,
  output DR_Clear
);

  wire and_2_out, and_3_out, and_4_out, and_out;

  and \and  (and_out, D0, T4);
  and and_2 (and_2_out, D1, T4);
  and and_3 (and_3_out, D2, T4);
  and and_4 (and_4_out, D6, T4);
  or or_1 (DR_Load, and_out, and_2_out, and_3_out, and_4_out);
  and and_5 (DR_Increment, D6, T5);

  assign DR_Clear = 1'b0;
endmodule

module AR_Control (
  input  D0,
  input  D1,
  input  D2,
  input  D3,
  input  D4,
  input  D5,
  input  D6,
  input  D7,
  input  T0,
  input  T1,
  input  T2,
  input  T3,
  input  T4,
  input  T5,
  input  T6,
  input  T7,
  input  T8,
  input  T9,
  input  T10,
  input  T11,
  input  T12,
  input  T13,
  input  T14,
  input  T15,
  input  I,
  output AR_Load,
  output AR_Increment,
  output AR_Clear
);

  wire and_1_out, not_1_out;

  not not_1 (not_1_out, D7);
  and and_1 (and_1_out, I, T3, not_1_out);
  or or_1 (AR_Load, T2, T0, and_1_out);
  and and_2 (AR_Increment, D5, T4);

  assign AR_Clear = 1'b0;
endmodule

module AC_Control (
  input  D0,
  input  D1,
  input  D2,
  input  D3,
  input  D4,
  input  D5,
  input  D6,
  input  D7,
  input  T0,
  input  T1,
  input  T2,
  input  T3,
  input  T4,
  input  T5,
  input  T6,
  input  T7,
  input  T8,
  input  T9,
  input  T10,
  input  T11,
  input  T12,
  input  T13,
  input  T14,
  input  T15,
  input  I,
  input  B0,
  input  B1,
  input  B2,
  input  B3,
  input  B4,
  input  B5,
  input  B6,
  input  B7,
  input  B8,
  input  B9,
  input  B10,
  input  B11,
  output AC_Load,
  output AC_Increment,
  output AC_Clear
);

  wire and_1_out, and_2_out, and_3_out, and_4_out, and_5_out, and_6_out, not_1_out, r;

  not not_1 (not_1_out, I);
  and and_1 (and_1_out, r, B7);
  and and_2 (and_2_out, D0, T5);
  and and_3 (and_3_out, D1, T5);
  and and_4 (and_4_out, D2, T5);
  and and_5 (and_5_out, r, B9);
  and and_6 (and_6_out, r, B8);
  and u_R (r, D7, not_1_out, T3);
  and and_7 (AC_Increment, r, B5);
  and and_8 (AC_Clear, r, B11);
  or or_1 (AC_Load, and_1_out, and_2_out, and_3_out, and_4_out, and_5_out, and_6_out);
endmodule

module SC (
  input  D0,
  input  D1,
  input  D2,
  input  D3,
  input  D4,
  input  D5,
  input  D6,
  input  D7,
  input  T0,
  input  T1,
  input  T2,
  input  T3,
  input  T4,
  input  T5,
  input  T6,
  input  T7,
  input  T8,
  input  T9,
  input  T10,
  input  T11,
  input  T12,
  input  T13,
  input  T14,
  input  T15,
  input  I,
  output SC_Clear
);

  wire and_1_out, and_2_out, and_3_out, not_1_out, or_1_out, or_2_out, R_out;

  or or_1 (or_1_out, D0, D1, D5, D2);
  and and_1 (and_1_out, T5, or_1_out);
  and and_2 (and_2_out, T4, or_2_out);
  or or_2 (or_2_out, D3, D4);
  and and_3 (and_3_out, T6, D6);
  not not_1 (not_1_out, I);
  and R (R_out, D7, not_1_out, T3);
  or or_3 (SC_Clear, and_1_out, and_2_out, and_3_out, R_out);
endmodule

module Memory_Control (
  input  D0,
  input  D1,
  input  D2,
  input  D3,
  input  D4,
  input  D5,
  input  D6,
  input  D7,
  input  T0,
  input  T1,
  input  T2,
  input  T3,
  input  T4,
  input  T5,
  input  T6,
  input  T7,
  input  T8,
  input  T9,
  input  T10,
  input  T11,
  input  T12,
  input  T13,
  input  T14,
  input  T15,
  input  I,
  output Memory_Read,
  output Memory_Write
);

  wire and_1_out, and_2_out, and_3_out, and_4_out, not_1_out, or_1_out, r;

  not not_1 (not_1_out, D7);
  and u_R (r, not_1_out, I, T3);
  or or_1 (or_1_out, D0, D1, D2, D6);
  and and_1 (and_1_out, D3, T4);
  and and_2 (and_2_out, D5, T4);
  and and_3 (and_3_out, D6, T6);
  and and_4 (and_4_out, T4, or_1_out);
  or or_2 (Memory_Read, T1, r, and_4_out);
  or or_3 (Memory_Write, and_1_out, and_2_out, and_3_out);
endmodule
